# Fritzing sketch Arduino_wiring (saved by Fritzing 0.9.1b)

parts:
  Part1 = Arduino Uno (Rev3)
  J2 = female pin header, 5 pins [form="♀ (female)"]
  CONN1 = USB connector [package=THT]
  LED1 = LED - 5mm [color="Red (633nm)" package="5 mm [THT]"]
  S1 = Pushbutton [package=THT]

nets:
  N1: Part1.D11_PWM/MOSI, LED1.anode
  N2: Part1.D12/MISO, S1.leg1
  N3: Part1.GND, J2.pin2, LED1.cathode, S1.leg0
  N4: Part1.D5_PWM, J2.pin3
  N5: Part1.D6_PWM, J2.pin4
  N6: J2.pin1, CONN1.5V
  N7: J2.pin5, CONN1.GND, CONN1.chassis5, CONN1.chassis6

notes:
  To printer
